# Fritzing sketch led (saved by Fritzing 0.9.3b)
breadboards: 1

parts:
  元件2 = Arduino Uno (Rev3)
  R1 = Resistor [tolerance=±5% resistance=220 package=THT]
  LED1 = LED - 5mm [color="Red (633nm)" package="5 mm [THT]"]

nets:
  N1: 元件2.GND, R1.Pin_0
  N2: 元件2.D2, LED1.anode
  N3: R1.Pin_1, LED1.cathode
